# Fritzing sketch connect relay (saved by Fritzing 1.0.0rc)

parts:
  Power_plug1 = Power plug
  U2 = V18ZA2P [package=v18za2p]
  KY-1 = Keyes Relay [package=THT]
  U3 = ESP8266-12e-tht [part_number=ESP8266-12E]

nets:
  N1: Power_plug1.GND, U2.-
  N2: Power_plug1.VCC, KY-1.NO
  N3: U2.+, KY-1.C
  N4: KY-1.signal, U3.connector19

custom parts:
  V18ZA2P: Varistor
  Keyes Relay: The Keyes 5V relay module is suitable for SCM development, home appliance control. It uses a 5V~12V TIL control signal which can control DC / AC signal.
